// Logisim project adder_test.circ as structural Verilog: 1 circuit, main circuit main
module main (
);

  wire button_2_out, button_3_out, button_4_out, \个位_q , \中间进位_out , \二位_q , \新个位_out , \新二位_out , \新进位_out ,
       \进位_q ;

  D_Flip_Flop \u_二位  (.Q(\二位_q ));  // open: clk, D, Qn, preset, en, reset
  D_Flip_Flop \u_个位  (.Q(\个位_q ));  // open: clk, D, Qn, preset, en, reset
  D_Flip_Flop \u_进位  (.Q(\进位_q ));  // open: clk, D, Qn, preset, en, reset
  and \u_中间进位  (\中间进位_out , \个位_q , \进位_q );
  LED led_1 (.in(\新进位_out ));
  and \u_新进位  (\新进位_out , \中间进位_out , \二位_q );
  xor \u_新二位  (\新二位_out , \中间进位_out , \二位_q );
  LED _2 (.in(\新二位_out ));
  xor \u_新个位  (\新个位_out , \个位_q , \进位_q );
  LED _1 (.in(\新个位_out ));
  Button _1_2 ();  // open: out
  Button _2_2 ();  // open: out
  Button _5 ();  // open: out
  Button _4 ();  // open: out
  Button _8 ();  // open: out
  Button _7 ();  // open: out
  Button _0 ();  // open: out
  Button button ();  // open: out
  Button button_2 (.out(button_2_out));
  Button button_3 (.out(button_3_out));
  Button button_4 (.out(button_4_out));
  Button _3 ();  // open: out
  Button _6 ();  // open: out
  Button _9 ();  // open: out
  Button button_5 ();  // open: out
  RAM ram_1 (.sel(button_2_out), .ld(button_3_out), .clr(button_4_out));  // open: addr, data, clk
endmodule
